# Fritzing sketch prac4 (saved by Fritzing 0.9.3b)
breadboards: 2

parts:
  IC1 = IC, DIP package, 20 pins [chip_label="latch 74373"]
  IC2 = IC, DIP package, 28 pins [chip_label="ram 62256"]
  Componente1 = Arduino Mega ADK (Rev3)
  IC3 = IC, DIP package, 14 pins [chip_label="OR 7432"]
  IC4 = IC, DIP package, 14 pins [chip_label="NOT 7404"]

nets:
  N1: IC1.pin1, IC1.pin10, IC2.pin1, IC2.pin2, IC2.pin14, IC2.pin23, IC2.pin26, Componente1.GND, IC4.pin7
  N2: IC1.pin2, IC2.pin10, Componente1.D22
  N3: IC1.pin3, IC2.pin11
  N4: IC1.pin4, IC2.pin12
  N5: IC1.pin5, IC2.pin9, Componente1.D23
  N6: IC1.pin6, IC2.pin8, Componente1.D24
  N7: IC1.pin7, IC2.pin13
  N8: IC1.pin8, IC2.pin15
  N9: IC1.pin9, IC2.pin7, Componente1.D25
  N10: IC1.pin11, Componente1.D39
  N11: IC1.pin12, IC2.pin6, Componente1.D26
  N12: IC1.pin13, IC2.pin16
  N13: IC1.pin14, IC2.pin17
  N14: IC1.pin15, IC2.pin5, Componente1.D27
  N15: IC1.pin16, IC2.pin4, Componente1.D28
  N16: IC1.pin17, IC2.pin18
  N17: IC1.pin18, IC2.pin19
  N18: IC1.pin19, IC2.pin3, Componente1.D29
  N19: IC1.pin20, IC2.pin28, Componente1.5V, IC4.pin14
  N20: IC2.pin20, IC3.pin3
  N21: IC2.pin22, Componente1.D40
  N22: IC2.pin24, Componente1.D36
  N23: IC2.pin25, Componente1.D37
  N24: IC2.pin27, Componente1.D41
  N25: Componente1.D31, Componente1.D34
  N26: Componente1.D33, IC4.pin1
  N27: IC3.pin4, IC4.pin2
